# Fritzing sketch Circuit Diagram (saved by Fritzing 0.9.4)
breadboards: 1

parts:
  ADC_PCF5891 = PCF8574 [package="DIP16 [THT]"]
  IR_Receiver = TSOP312.., 314.. [package=THT]
  Sparkfun_Sound_Detector = Breakout Board for Electret Microphone
  IR_Led = LTE-302 [package=lte-302]
  NPN = NPN-Transistor [package="SOT-23 [SMD]"]
  R1 = Resistor [tolerance=±5% resistance=220 package="0402 [SMD]"]
  R2 = Resistor [tolerance=±5% resistance=10 package="0402 [SMD]"]
  R3 = Resistor [tolerance=±5% resistance=220k package="0402 [SMD]"]
  Raspberry_Pi_4 = Raspberry Pi B+
  R4 = Resistor [tolerance=±5% resistance=10 package="0402 [SMD]"]
  R5 = Resistor [tolerance=±5% resistance=10 package="0402 [SMD]"]
  Led = LED - 3mm [color="Red (633nm)" package="3 mm [THT]"]

nets:
  N1: ADC_PCF5891.A0, Sparkfun_Sound_Detector.AUD
  GND: ADC_PCF5891.P1, ADC_PCF5891.P2, ADC_PCF5891.P3, ADC_PCF5891.GND, ADC_PCF5891.P7, ADC_PCF5891.INT, IR_Receiver.GND, Sparkfun_Sound_Detector.GND, NPN.2, Led.cathode
  N2: ADC_PCF5891.P4, Raspberry_Pi_4.GPIO2, R4.Pin_0
  N3: ADC_PCF5891.P5, Raspberry_Pi_4.GPIO3, R5.Pin_0
  3.3V: ADC_PCF5891.SCL, R4.Pin_1, R5.Pin_1
  5V: ADC_PCF5891.VCC, IR_Receiver.Vs, Sparkfun_Sound_Detector.VCC, R3.Pin_0
  N4: IR_Receiver.Data, Raspberry_Pi_4.GPIO17
  N5: IR_Led.A, R3.Pin_1
  N6: IR_Led.C, NPN.1
  N7: NPN.0, R2.Pin_1
  N8: R1.Pin_0, Led.anode
  N9: R1.Pin_1, Raspberry_Pi_4.GPIO5
  N10: R2.Pin_0, Raspberry_Pi_4.GPIO18
